// Logisim project archiMinimale.circ as structural Verilog: 1 circuit, main circuit main
module main (
  input  H,
  input  Raz
);

  wire branch, emem, ereg, immrt, not_1_out, not_2_out, registerfile_1_p8, rtrd, tunnel, ualmem;
  wire [3:0] op;
  wire [4:0] multiplexer_1_out, num_rd, num_rs, num_rt, shamt;
  wire [5:0] co, nf;
  wire [31:0] adder_1_p3, imm32, mips_ram_1_p7, multiplexer_3_out, pc, res, rs, rt, w;

  not not_1 (not_1_out, ereg);
  // Adder adder_1: pin names not known; wires that end beside it: 32'h4, pc, adder_1_p3
  Register #(.width(32), .trigger("falling")) register_1 (.D(adder_1_p3), .en(1'b1), .Q(pc), .clk(H), .clr(Raz));
  Multiplexer #(.width(5), .enable("false")) multiplexer_1 (
    .in0(num_rt), .in1(num_rd), .out(multiplexer_1_out), .sel(rtrd));
  // RegisterFile registerfile_1: pin names not known; wires that end beside it: w, H, not_1_out, multiplexer_1_out, num_rs, num_rt, Raz, registerfile_1_p8, rt
  // MIPS_RAM mips_ram_1: pin names not known; wires that end beside it: res[19:0], rt, emem, 1'b1, H, Raz, mips_ram_1_p7
  Multiplexer #(.width(32), .enable("false")) multiplexer_2 (.in0(res), .in1(mips_ram_1_p7), .out(w), .sel(ualmem));
  Multiplexer #(.width(32), .enable("false")) multiplexer_3 (
    .in0(imm32), .in1(rt), .out(multiplexer_3_out), .sel(immrt));
  // PLA pla_1: pin names not known; wires that end beside it: co, {emem, ereg, branch, ualmem, immrt, rtrd}
  // MIPS_ALU mips_alu_1: pin names not known; wires that end beside it: registerfile_1_p8, multiplexer_3_out, op, tunnel, res
  // MIPSProgramROM mipsprogramrom_1: pin names not known; wires that end beside it: pc, {co, num_rs, num_rt, num_rd, shamt, nf}
  // Probe on {co, num_rs, num_rt, num_rd, shamt, nf}
  // Probe on res
  // PLA PLA_2: pin names not known; wires that end beside it: {nf, co}, op
  // Probe on rtrd
  // Probe on immrt
  // Probe on ualmem
  // Probe on branch
  // Probe on not_2_out
  not not_2 (not_2_out, ereg);
  // Probe on emem
  // Probe on op
  assign imm32 = {{16{1'b0}}, {num_rd, shamt, nf}};  // Bit_Extender bit_extender_1
  // Probe on pc
  // Probe on co
  // Probe on num_rs
  // Probe on rs
  // Probe on num_rt
  // Probe on rt
  // Probe on num_rd
  // Probe on shamt
  // Probe on nf
  // Probe on imm32

  // Other names for the same wires on the sheet: _0 = Raz

  // Notes on the sheet:
  //   détermination de la prochaine instruction (pc)
  //   mémoire de donnée
  //   Meh
  //   commandes
  //   décomposition de l'opération MIPS
  //   vérifications
endmodule
